# Fritzing sketch adbcvc (saved by Fritzing 0.9.3b)

parts:
  LoRa_Module1 = Ra-01 - LoRa Module SX1278 [part_number=SX1278]
  KY-1 = Keyes Relay [package=THT]
  LED1 = LEDs [package=led10mm]
  Part2 = Arduino Nano (Rev3.0)
  DHT11_1 = DHT22_BLACK_PCB
  KY-2 = Keyes Relay [package=THT]
  M1 = DC Motor
  WATER_PUMP1 = prefix0000  # not connected
  부품3 = FC-28 Soil Hygrometer Module
  부품4 = FC-28 Soil Hygrometer Module - Probe
  부품5 = FC-28 Soil Hygrometer Module
  R1 = Photocell (LDR) [package=THT]

nets:
  N1: LoRa_Module1.GND, Part2.D12/MISO
  N2: LoRa_Module1.NSS, Part2.D11/MOSI
  N3: LoRa_Module1.MOSI, Part2.D10
  N4: LoRa_Module1.MISO, Part2.D9
  N5: LoRa_Module1.SCK, Part2.D8
  3.3V: LoRa_Module1.3.3V, Part2.3V3
  N6: LoRa_Module1.DIO0, Part2.D13/SCK
  N7: KY-1.signal, Part2.D3
  N8: LED1.A, Part2.D4
  N9: Part2.D2, DHT11_1.connector9
  N10: Part2.D5, KY-2.signal
  N11: Part2.GND, DHT11_1.connector6, KY-2.ground
  N12: Part2.5V, DHT11_1.connector5, KY-2.power
  N13: Part2.A1, 부품3.AO
  N14: Part2.A0, 부품5.AO
  N15: KY-2.NC, M1.pin_1
  N16: KY-2.C, M1.pin_2
  N17: 부품3.POS, R1.pin_1
  N18: 부품3.NEG, R1.pin_0
  N19: 부품4.POS, 부품5.POS
  N20: 부품4.NEG, 부품5.NEG

custom parts:
  Ra-01 - LoRa Module SX1278: The Ra-01 LoRa Module featuring the SX1278 engine by Semtech. Module by AI-Thinker. Module (Ra-01) specifications from: https://www.banggood.com/Ra-01-Smart-Electronics-SX1278-LoRa-Spread-Spectrum-Wireless-Module-Ultra-Far-10KM-433M-p-1130769.html Description: Power supply: DC1.8-3.7V(3.3V) Chip: SX1278 Frequency: 433Mhz Operating temperature: -40~+85°C On Sheild Description (may vary by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
  Keyes Relay: The Keyes 5V relay module is suitable for SCM development, home appliance control. It uses a 5V~12V TIL control signal which can control DC / AC signal.
  LEDs: LEDs Standard schematic elements and footprints for 5mm, 3mm, 1206, and 0603 sized LEDs. 5mm - Spark Fun Electronics SKU : COM-00529 (and others)
  FC-28 Soil Hygrometer Module: The FC-28 is a soil hygrometer module that uses the Texas Instruments LM393 comparator chip to provide an analog measurement of soil humidity. The digital output is high when soil moisture is over a certain threshold, as determined by adjusting the potentiometer.
  FC-28 Soil Hygrometer Module - Probe: The FC-28 is a soil hygrometer module that uses the Texas Instruments LM393 comparator chip to provide an analog measurement of soil humidity.
